# Fritzing sketch breadboard_older (saved by Fritzing 0.9.3b)
breadboards: 1

parts:
  L298N1 = L298N DC motor driver
  L298N2 = L298N DC motor driver
  M5 = Hobby Gearmotor with 48:1 gearbox [part_number=ROB-13302]
  M6 = Hobby Gearmotor with 48:1 gearbox [part_number=ROB-13302]
  M7 = Hobby Gearmotor with 48:1 gearbox [part_number=ROB-13302]
  M8 = Hobby Gearmotor with 48:1 gearbox [part_number=ROB-13302]
  Part1 = Arduino Uno (Rev3) - ICSP
  Part2 = Bluetooth HC-05 Macho
  VCC1 = 4 x AAA Battery Mount

nets:
  N1: L298N1.OUT1, M5.pin_2
  N2: L298N1.OUT2, M5.pin_1
  N3: L298N1.OUT3, M8.pin_2
  N4: L298N1.OUT4, M8.pin_1
  12V: L298N1.12V, L298N2.12V, Part1.VIN, VCC1.+
  GND: L298N1.GND, L298N2.GND, Part1.GND, Part2.GND, VCC1.-
  5V: L298N1.5V#7, L298N2.5V, Part1.5V, Part2.VCC
  N5: L298N1.5V#9, L298N1.ENA, Part1.D5_PWM
  N6: L298N1.5V#10, L298N1.ENB, Part1.D6_PWM
  N7: L298N1.IN1, Part1.D2
  N8: L298N1.IN2, Part1.D4
  N9: L298N1.IN3, Part1.D7
  N10: L298N1.IN4, Part1.D8
  N11: L298N2.OUT1, M6.pin_2
  N12: L298N2.OUT2, M6.pin_1
  N13: L298N2.OUT3, M7.pin_2
  N14: L298N2.OUT4, M7.pin_1
  N15: L298N2.ENA, Part1.D9_PWM
  N16: L298N2.ENB, Part1.ICSP_MOSI, Part1.D11_PWM/MOSI
  N17: L298N2.IN1, Part1.D12/MISO
  N18: L298N2.IN2, Part1.D13/SCK
  N19: L298N2.IN3, Part1.A3
  N20: L298N2.IN4, Part1.A4/SDA
  N21: Part1.D10_PWM/SS, Part2.TXD
  N22: Part1.D3_PWM, Part2.RXD

notes:
  Breadboard sketch for a bluetooth module controlled car

custom parts:
  L298N DC motor driver: 2x DC motor driver with 78M05 positive voltage regulator (7..35 V) L298N: max 46 V, 2 A Set 5 V Enable jumper to enable 5 V regultor (needed for the L298N) and +5 V output at screw terminal or supply external +5 V at screw terminal Set ENA and/or ENB to +5 V to enable motor permanently or supply ENA and/or ENB with PWM signal IN1 and IN2 set rotation directory for motor A (OUT1/OUT2) IN2 and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
